// Logisim project new_CPU.circ as structural Verilog: 4 circuits, main circuit main
module main (
  output [3:0] out_1,
  output [3:0] out_2,
  output [3:0] out_3,
  output [3:0] out_4,
  output [3:0] out_5,
  output [3:0] out_6
);

  wire Adress, ALU, ALUCarry, ALULogic, and_1_out, and_2_out, clock_1_out, demultiplexer_1_out1, Digit,
       DoJump, FlagWrite, Jump, not_1_out, not_2_out, not_3_out, or_1_out, w, Write;
  wire [1:0] myalu_1_aeqb, register_1_q;
  wire [3:0] ALUop, multiplexer_1_out, Operation, Outp, RAMDigit;

  and and_1 (and_1_out, Digit, Adress);
  Demultiplexer #(.disabled("Z")) demultiplexer_1 (.out0(w), .out1(demultiplexer_1_out1), .in(Write), .sel(and_1_out));
  Multiplexer #(.disabled("Z"), .width(4)) multiplexer_1 (
    .in0(out_3), .in1(out_4), .out(multiplexer_1_out), .sel(not_1_out));
  not not_1 (not_1_out, Digit);
  RAM #(.addrWidth(4), .dataWidth(4)) ram_1 (
    .addr(multiplexer_1_out), .we(demultiplexer_1_out1), .oe(1'b1), .clk(demultiplexer_1_out1), .din(out_1),
    .dout(RAMDigit));
  MyALU myalu_1 (
    .Cin(ALUCarry), .Operation(ALUop), .A(out_3), .B(out_4), .M(ALULogic), .Outp(Outp),
    .AeqB(myalu_1_aeqb[0]), .Sign(myalu_1_aeqb[1]));
  Register #(.width(2)) register_1 (.D(myalu_1_aeqb), .clk(and_2_out), .Q(register_1_q));  // open: en, clr
  and and_2 (and_2_out, FlagWrite, not_2_out);
  not not_2 (not_2_out, clock_1_out);
  Clock clock_1 (.out(clock_1_out));
  OperationDecoder operationdecoder_1 (
    .Operation(Operation), .Digit(Digit), .Jump(Jump), .ALULogic(ALULogic), .ALU(ALU), .ALUCarry(ALUCarry),
    .FlagWrite(FlagWrite), .Adress(Adress), .ALUop(ALUop));
  nor nor_1 (Write, clock_1_out, Jump);
  or or_1 (or_1_out, register_1_q[1], register_1_q[0]);
  not not_3 (not_3_out, register_1_q[0]);
  Multiplexer #(.disabled("Z"), .select(2)) multiplexer_2 (
    .in0(register_1_q[0]), .in1(register_1_q[1]), .in2(or_1_out), .in3(not_3_out), .out(DoJump),
    .sel(ALUop[1:0]));
  PC pc_1 (.Clock(clock_1_out), .Operation(Operation), .A(out_5), .B(out_6));  // open: ClockWait, CA

  // Other names for the same wires on the sheet: A[3:0] = out_3; A_in[3:0] = out_5; B[3:0] = out_4; B_in[3:0] = out_6;
  //   Data[3:0] = out_1; ID[3:0] = out_2
endmodule

module MyALU (
  input  Cin,
  input  [3:0] Operation,
  input  [3:0] A,
  input  [3:0] B,
  input  M,
  output [3:0] Outp,
  output AeqB,
  output Sign
);

  wire n74181_1_p13, n74181_1_p14, n74181_1_p16, n74181_1_p18, not_2_out;

  // _74181 74181_1: pin names not known; wires that end beside it: B[0], A[1], A[0], B[1], Operation[3], A[2], Operation[2], B[2], Operation[1], A[3], Operation[0], B[3], n74181_1_p13, n74181_1_p14, M, n74181_1_p16, Outp[0], n74181_1_p18, Outp[1], AeqB, Outp[2], Outp[3]
  and and_1 (Sign, n74181_1_p14, not_2_out);
  not not_1 (n74181_1_p13, Cin);
  not not_2 (not_2_out, AeqB);

  // Notes on the sheet:
  //   Cout
  //   Pn
endmodule

module PC (
  input  Clock,
  input  ClockWait,
  output [7:0] CA,
  output [3:0] Operation,
  output [3:0] A,
  output [3:0] B
);

  wire ClockUpd, not_1_out;
  wire [7:0] controlled_buffer_1_out, counter_1_q;

  Counter #(.ongoal("stay")) counter_1 (.clk(ClockUpd), .D(CA), .Q(counter_1_q));  // open: clr, load, up, count, carry
  assign controlled_buffer_1_out = not_1_out ? counter_1_q : 8'bz;  // Controlled_Buffer controlled_buffer_1
  ROM #(.dataWidth(12)) rom_1 (.addr(controlled_buffer_1_out), .data({B, A, Operation}));
  not not_1 (not_1_out, ClockWait);
  and and_1 (ClockUpd, not_1_out, Clock);

  // Other names for the same wires on the sheet: CurrAdress[7:0] = CA

  // Notes on the sheet:
  //   contents of rom_1 (hex, n*v repeats v):
  //   0 151 144 a45
endmodule

module OperationDecoder (
  input  [3:0] Operation,
  output Digit,
  output Jump,
  output ALULogic,
  output ALU,
  output ALUCarry,
  output FlagWrite,
  output Adress,
  output [3:0] ALUop
);

  wire [15:7] rom_1_data;

  ROM #(.addrWidth(4), .dataWidth(16)) rom_1 (
    .addr(Operation), .data({rom_1_data, Adress, FlagWrite, ALUCarry, ALU, ALULogic, Jump, Digit}));

  assign ALUop = Operation;

  // Notes on the sheet:
  //   contents of rom_1 (hex, n*v repeats v):
  //   0 1 41 40 c 0 38 0 0 8 0 0 4*2
endmodule
